# Fritzing sketch 3DScanner (saved by Fritzing 1.0.2b)
breadboards: 2

parts:
  Part1 = Arduino Mega 2560 (Rev3)
  M1 = Stepper Motor - Bipolar
  Pololu_A1 = Pololu A4988 [package=SO16]
  C6 = Electrolytic Capacitor [capacitance=100μF voltage=50V package="0807 [SMD, electrolytic]"]
  M2 = Stepper Motor - Bipolar
  Pololu_A2 = Pololu A4988 [package=SO16]
  C7 = Electrolytic Capacitor [capacitance=100μF voltage=50V package="0807 [SMD, electrolytic]"]
  J1 = Basic Servo
  S1 = Pushbutton [package="[THT]"]
  S2 = Pushbutton [package="[THT]"]
  S3 = Pushbutton [package="[THT]"]
  R1 = Resistor [tolerance=±5% resistance=100 package="1206 [SMD]"]
  R2 = Resistor [tolerance=±5% resistance=100 package="1206 [SMD]"]
  R3 = Resistor [tolerance=±5% resistance=100 package="1206 [SMD]"]

nets (from the schematic view):
  ground: Part1.GND, Pololu_A1.GND#8, Pololu_A2.GND#8, J1.gnd, R1.Pin_0, R2.Pin_0, R3.Pin_0
  N1: Part1.D13_PWM, S1.Pin_3, S1.Pin_4
  N2: Part1.D12_PWM, S2.Pin_3, S2.Pin_4
  N3: Part1.D11_PWM, S3.Pin_3, S3.Pin_4
  pin 9: Part1.D9_PWM, J1.pulse
  3.3V: Part1.3V3, J1.vcc
  pin 2: Part1.D2_PWM, Pololu_A2.STEP
  pin 3: Part1.D3_PWM, Pololu_A2.DIR
  pin 5: Part1.D5_PWM, Pololu_A1.STEP
  pin 6: Part1.D6_PWM, Pololu_A1.DIR
  5v: Part1.5V, Pololu_A1.VDD, Pololu_A2.VDD, S1.Pin_1, S1.Pin_2, S2.Pin_1, S2.Pin_2, S3.Pin_1, S3.Pin_2, R1.Pin_1, R2.Pin_1, R3.Pin_1
  N4: M1.A, Pololu_A1.2B
  N5: M1.C, Pololu_A1.2A
  N6: M1.B, Pololu_A1.1A
  N7: M1.D, Pololu_A1.1B
  N8: Pololu_A1.RESET, Pololu_A1.SLEEP
  GND: Pololu_A1.GND#14, C6.-, Pololu_A2.GND#14, C7.-
  12V: Pololu_A1.VMOT, C6.+, Pololu_A2.VMOT, C7.+
  N9: M2.A, Pololu_A2.2B
  N10: M2.C, Pololu_A2.2A
  N11: M2.B, Pololu_A2.1A
  N12: M2.D, Pololu_A2.1B
  N13: Pololu_A2.RESET, Pololu_A2.SLEEP

// code stored in the sketch: ScennerCode.ino
// Define pins for both stepper motors
#define stepPin1 2    // First stepper motor step pin
#define dirPin1 3     // First stepper motor direction pin
#define stepPin2 5    // Second stepper motor step pin
#define dirPin2 6     // Second stepper motor direction pin


// Steps calculation for 1.8° motor (200 steps per revolution)
const int STEPS_PER_REV = 200;  // Full rotation
const int STEPS_18_DEG = 10;    // (200 * 18) / 360 = 10 steps


int segmentCount = 0;


void setup() {
  pinMode(stepPin1, OUTPUT); 
  pinMode(dirPin1, OUTPUT);
  pinMode(stepPin2, OUTPUT); 
  pinMode(dirPin2, OUTPUT);
  Serial.begin(9600);
  Serial.println("Starting motor sequence...");
}


void move_motor(int stepPin, int steps, int speed) {
  Serial.print("Moving steps: ");
  Serial.println(steps);


  for(int i = 0; i < steps; i++) {
    digitalWrite(stepPin, HIGH);
    delayMicroseconds(speed);
    digitalWrite(stepPin, LOW);
    delayMicroseconds(speed);
  }
}


void loop() {
  // Move second motor 18 degrees
  Serial.print("Moving second motor 18 degrees - Segment ");
  Serial.println(segmentCount + 1);



  move_motor(stepPin2, STEPS_18_DEG, 1000);


  segmentCount++;
  Serial.println("Take a fucking picture"); // this Triggers the camera code to take a pic


  // If we completed 360 degrees (20 segments of 18 degrees)
  if(segmentCount >= 20) {
    Serial.println("360 degrees completed - Moving first motor 360 degrees");


    // Move first motor 360 degrees (full rotation = 200 steps)
    // Breaking it into 4 segments of 50 steps each for smoother movement
    for(int i = 0; i < 4; i++) {
      move_motor(stepPin1, 50, 1500);  // 50 steps × 4 = 200 steps (full rotation)
    }


    segmentCount = 0;  // Reset counter
    Serial.println("Sequence completed, waiting 2 seconds...");
    delay(2000);
  }


  delay(1000);  // Wait between movements
}
